# Fritzing sketch oled-128x64-tester (saved by Fritzing 0.9.4)

parts:
  Part1 = Adafruit Metro with Headers [part_number="Adafruit #2488"]
  OLED1 = OLED 128x64 I2C Monochrome Display

nets:
  N1: Part1.AD5/SCL, OLED1.SCK
  N2: Part1.AD4/SDA, OLED1.SDA
  +5V: Part1.+5V, OLED1.VDD
  GND: Part1.GND, OLED1.GND

custom parts:
  Adafruit Metro with Headers: We sure love the ATmega328 here at Adafruit, and we use them a lot for our own projects. The processor has plenty of GPIO, Analog inputs, hardware UART SPI and I2C, timers and PWM galore - just enough for most simple projects. When we need to go small, we use a Pro Trinket 3V or 5V, but when size isn't as much of a concern, and an USB-serial converter is required, we reach for an Adafruit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
